# Fritzing sketch 5V_project (saved by Fritzing 1.0.1rc)
stripboards: 1

parts:
  Mod1 = Raspberry Pi Pico
  J1 = JST-B3P-VH [part_number=JST-B3P-VH package=THT]
  U1 = Mini-360 DC-DC Buck converter [package=THT]
  U2 = TXS0108 [part_number=TXS0108EPW package=TSSOP]

nets:
  N1: Mod1.pin_4, U2.A4
  N2: Mod1.pin_33, Mod1.pin_42, U1.OUT-, U2.GND
  N3: Mod1.pin_36, U2.VccA, U2.OE
  N4: Mod1.pin_40, U1.OUT+, U2.VccB
  N5: J1.pin2, U1.IN+
  N6: J1.pin1, U2.B4
  N7: J1.pin3, U1.IN-

notes:
  Check your lights connector to confirm the order of connections!
  Adjust output to 5V before connecting the Pico!
  Colors:
  Black: GND
  Red/White: 12V
  Red: 5V
  Yellow: 3.3V
  Blue: Data (3.3V level)
  Blue/White: Data (5V level)

custom parts:
  Raspberry Pi Pico: Raspberry Pi Pico. Based around the RP2040 microcontroller the Pico is a low cost microcontroller device bringing Raspberry Pi quality, cost, and easy of use to the microcontroller space. Jan 2021, Split part in to two versions: tht (this one) and SMD. This one will drill holes for a .1 in header in pcb to allow plugging in the module as well as providing pads to solder the module to the top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
  Mini-360 DC-DC Buck converter: Mini-360 DC-DC Buck converter. Tiny buck step down voltage converter, input voltage 4.75 to 23V output 1 to 17V adjustable. Available from ebay and the like.
  TXS0108: This 8-bit non-inverting translator uses two separate configurable power-supply rails. The A port tracks the VCCA pin supply voltage. The VCCA pin accepts any supply voltage between 1.2 V and 3.6 V. The B port tracks the VCCB pin supply voltage. The VCCB pin accepts any supply voltage between 1.65 V and 5.5 V. Two input supply pins allows for low Voltage bidirectional translation between any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
