# Fritzing sketch project (saved by Fritzing 1.0.1rc)

parts:
  Mod1 = Raspberry Pi Pico
  J1 = JST-B3P-VH [part_number=JST-B3P-VH package=THT]
  U1 = Mini-360 DC-DC Buck converter [package=THT]

nets:
  N1: Mod1.pin_4, J1.pin1
  N2: Mod1.pin_28, Mod1.pin_38, Mod1.pin_42, U1.OUT-
  N3: Mod1.pin_40, U1.OUT+
  N4: J1.pin2, U1.IN+
  N5: J1.pin3, U1.IN-

notes:
  Check your lights connector to confirm the order of connections!
  Adjust output to 5V before connecting the Pico!
  Colors:
  Black: GND
  Red/White: 12V
  Red: 5V
  Blue: Data (3.3V level)

custom parts:
  Raspberry Pi Pico: Raspberry Pi Pico. Based around the RP2040 microcontroller the Pico is a low cost microcontroller device bringing Raspberry Pi quality, cost, and easy of use to the microcontroller space. Jan 2021, Split part in to two versions: tht (this one) and SMD. This one will drill holes for a .1 in header in pcb to allow plugging in the module as well as providing pads to solder the module to the top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
  Mini-360 DC-DC Buck converter: Mini-360 DC-DC Buck converter. Tiny buck step down voltage converter, input voltage 4.75 to 23V output 1 to 17V adjustable. Available from ebay and the like.
